# Fritzing sketch poki_v2 (saved by Fritzing 0.9.8b)
perfboards: 1

parts:
  Part2 = Arduino Uno (Rev3) - ICSP  # not connected
  Part3 = Arduino Prototyping Shield  # not connected
  M1 = DC Motor  # not connected
  M2 = DC Motor  # not connected
  BAT1 = Battery Holders [package=battery-aa]
  BAT2 = Battery Holders [package=battery-aa]  # not connected
  BAT3 = Battery Holders [package=battery-aa]  # not connected
  BAT4 = Battery Holders [package=battery-aa]
  J1 = Infrared Proximity Sensor  # not connected
  J2 = Infrared Proximity Sensor  # not connected
  J3 = Infrared Proximity Sensor  # not connected
  R1 = Trimmer Potentiometer [maximum_resistance=10kΩ package=THT]  # not connected

nets:
  N1: BAT1.-, BAT4.+
  N2: BAT1.+, BAT4.-
