# Fritzing sketch Untitled Sketch 2 (saved by Fritzing 0.9.3b)

parts:
  M1 = DC Motor  # not connected
  M2 = DC Motor  # not connected
  Arduino_One_Controller = Arduino Uno (Rev3) - ICSP  # not connected
  IR_Sensor_Left = Infrared Proximity Sensor
  Potentiometer_IR_Left = Trimmer Potentiometer [maximum_resistance=10kΩ package=THT]
  IR_Sensor_Center = Infrared Proximity Sensor
  Potentiometer_IR_Center = Trimmer Potentiometer [maximum_resistance=10kΩ package=THT]
  IR_Sensor_Right = Infrared Proximity Sensor
  Potentiometer_IR_Right = Trimmer Potentiometer [maximum_resistance=10kΩ package=THT]

nets:
  N1: IR_Sensor_Left.Vout, Potentiometer_IR_Left.leg2
  N2: IR_Sensor_Left.GND, Potentiometer_IR_Left.wiper
  N3: IR_Sensor_Left.Vcc, Potentiometer_IR_Left.leg1
  N4: IR_Sensor_Center.Vout, Potentiometer_IR_Center.leg2
  N5: IR_Sensor_Center.GND, Potentiometer_IR_Center.wiper
  N6: IR_Sensor_Center.Vcc, Potentiometer_IR_Center.leg1
  N7: IR_Sensor_Right.Vout, Potentiometer_IR_Right.leg2
  N8: IR_Sensor_Right.GND, Potentiometer_IR_Right.wiper
  N9: IR_Sensor_Right.Vcc, Potentiometer_IR_Right.leg1
